// Logisim project ALU.circ as structural Verilog: 1 circuit, main circuit main
module main (
  input  d1_1,
  input  d2_1,
  input  d4_1,
  input  d8_1,
  input  d16_1,
  input  d32_1,
  input  d64_1,
  input  d128_1,
  input  d1_2,
  input  d2_2,
  input  d4_2,
  input  d8_2,
  input  d16_2,
  input  d32_2,
  input  d64_2,
  input  d128_2,
  input  Addition,
  input  Subtraction,
  input  Multiplication,
  input  Division
);

  wire and_1_out, and_2_out, and_3_out, and_4_out, and_5_out, and_6_out, and_7_out, and_8_out, and_9_out,
       and_10_out, and_11_out, and_12_out, and_13_out, and_14_out, and_15_out, and_16_out, and_17_out,
       and_18_out, and_19_out, and_20_out, and_21_out, and_22_out, and_23_out, and_24_out, and_25_out,
       and_26_out, and_27_out, and_28_out, and_29_out, and_30_out, and_31_out, and_32_out, and_33_out,
       and_34_out, and_35_out, and_36_out, and_37_out, and_38_out, and_39_out, and_40_out, and_41_out,
       and_42_out, and_43_out, and_44_out, and_45_out, and_46_out, and_47_out, and_48_out, and_49_out,
       and_50_out, and_51_out, and_52_out, and_53_out, and_54_out, and_55_out, and_56_out, and_57_out,
       and_58_out, and_59_out, and_60_out, and_61_out, and_62_out, not_1_out, not_2_out, not_3_out,
       not_4_out, not_5_out, not_6_out, not_7_out, not_8_out, not_9_out, not_10_out, not_11_out, not_12_out,
       not_13_out, not_14_out, not_15_out, or_1_out, or_2_out, or_3_out, or_4_out, or_5_out, or_6_out,
       or_7_out, or_8_out, or_9_out, or_10_out, or_11_out, or_12_out, or_13_out, or_14_out, xor_1_out,
       xor_2_out, xor_3_out, xor_4_out, xor_5_out, xor_6_out, xor_7_out, xor_8_out, xor_9_out, xor_10_out,
       xor_11_out, xor_12_out, xor_13_out, xor_14_out, xor_15_out, xor_16_out, xor_17_out, xor_18_out,
       xor_19_out, xor_20_out, xor_21_out, xor_22_out, xor_23_out, xor_24_out, xor_25_out, xor_26_out,
       xor_27_out, xor_28_out, xor_29_out, xor_30_out;

  and and_1 (and_1_out, Addition, d128_1);
  and and_2 (and_2_out, Addition, d128_2);
  and and_3 (and_3_out, Addition, d64_1);
  and and_4 (and_4_out, Addition, d64_2);
  and and_5 (and_5_out, Addition, d32_1);
  and and_6 (and_6_out, Addition, d32_2);
  and and_7 (and_7_out, Addition, d16_1);
  and and_8 (and_8_out, Addition, d8_1);
  and and_9 (and_9_out, Addition, d16_2);
  and and_10 (and_10_out, Addition, d8_2);
  and and_11 (and_11_out, Addition, d4_1);
  and and_12 (and_12_out, Addition, d4_2);
  xor xor_1 (xor_1_out, and_29_out, and_28_out);
  and and_13 (and_13_out, and_29_out, and_28_out);
  xor xor_2 (xor_2_out, and_15_out, and_14_out);
  xor xor_3 (xor_3_out, and_12_out, and_11_out);
  xor xor_4 (xor_4_out, and_10_out, and_8_out);
  xor xor_5 (xor_5_out, and_9_out, and_7_out);
  xor xor_6 (xor_6_out, and_6_out, and_5_out);
  xor xor_7 (xor_7_out, and_4_out, and_3_out);
  xor xor_8 (xor_8_out, and_2_out, and_1_out);
  and and_14 (and_14_out, Addition, d2_1);
  and and_15 (and_15_out, Addition, d2_2);
  xor xor_9 (xor_9_out, xor_2_out, and_13_out);
  and and_16 (and_16_out, and_13_out, xor_2_out);
  and and_17 (and_17_out, and_15_out, and_14_out);
  and and_18 (and_18_out, or_1_out, xor_3_out);
  and and_19 (and_19_out, and_12_out, and_11_out);
  and and_20 (and_20_out, or_2_out, xor_4_out);
  and and_21 (and_21_out, and_10_out, and_8_out);
  and and_22 (and_22_out, or_3_out, xor_5_out);
  and and_23 (and_23_out, and_9_out, and_7_out);
  and and_24 (and_24_out, or_4_out, xor_6_out);
  and and_25 (and_25_out, and_6_out, and_5_out);
  and and_26 (and_26_out, or_6_out, xor_8_out);
  and and_27 (and_27_out, and_2_out, and_1_out);
  and and_28 (and_28_out, Addition, d1_1);
  and and_29 (and_29_out, Addition, d1_2);
  xor xor_10 (xor_10_out, xor_3_out, or_1_out);
  xor xor_11 (xor_11_out, xor_4_out, or_2_out);
  xor xor_12 (xor_12_out, xor_5_out, or_3_out);
  xor xor_13 (xor_13_out, xor_6_out, or_4_out);
  xor xor_14 (xor_14_out, xor_7_out, or_5_out);
  and and_30 (and_30_out, or_5_out, xor_7_out);
  and and_31 (and_31_out, and_4_out, and_3_out);
  xor xor_15 (xor_15_out, xor_8_out, or_6_out);
  or or_1 (or_1_out, and_16_out, and_17_out);
  or or_2 (or_2_out, and_18_out, and_19_out);
  or or_3 (or_3_out, and_20_out, and_21_out);
  or or_4 (or_4_out, and_22_out, and_23_out);
  or or_5 (or_5_out, and_24_out, and_25_out);
  or or_6 (or_6_out, and_30_out, and_31_out);
  or or_7 (or_7_out, and_26_out, and_27_out);
  and and_32 (and_32_out, Subtraction, d128_1);
  and and_33 (and_33_out, Subtraction, d64_1);
  and and_34 (and_34_out, Subtraction, d128_2);
  and and_35 (and_35_out, Subtraction, d64_2);
  and and_36 (and_36_out, Subtraction, d32_1);
  and and_37 (and_37_out, Subtraction, d32_2);
  and and_38 (and_38_out, Subtraction, d16_1);
  and and_39 (and_39_out, Subtraction, d16_2);
  and and_40 (and_40_out, Subtraction, d8_1);
  and and_41 (and_41_out, Subtraction, d4_1);
  and and_42 (and_42_out, Subtraction, d8_2);
  and and_43 (and_43_out, Subtraction, d4_2);
  not not_1 (not_1_out, and_48_out);
  and and_44 (and_44_out, Subtraction, d2_1);
  and and_45 (and_45_out, Subtraction, d2_2);
  xor xor_16 (xor_16_out, and_48_out, and_47_out);
  and and_46 (and_46_out, not_1_out, and_47_out);
  xor xor_17 (xor_17_out, and_45_out, and_44_out);
  not not_2 (not_2_out, and_45_out);
  not not_3 (not_3_out, and_45_out);
  xor xor_18 (xor_18_out, and_43_out, and_41_out);
  not not_4 (not_4_out, and_43_out);
  not not_5 (not_5_out, and_43_out);
  xor xor_19 (xor_19_out, and_42_out, and_40_out);
  not not_6 (not_6_out, and_42_out);
  not not_7 (not_7_out, and_42_out);
  xor xor_20 (xor_20_out, and_39_out, and_38_out);
  not not_8 (not_8_out, and_39_out);
  not not_9 (not_9_out, and_39_out);
  xor xor_21 (xor_21_out, and_37_out, and_36_out);
  not not_10 (not_10_out, and_37_out);
  not not_11 (not_11_out, and_37_out);
  xor xor_22 (xor_22_out, and_35_out, and_33_out);
  not not_12 (not_12_out, and_35_out);
  not not_13 (not_13_out, and_35_out);
  xor xor_23 (xor_23_out, and_34_out, and_32_out);
  not not_14 (not_14_out, and_34_out);
  not not_15 (not_15_out, and_34_out);
  and and_47 (and_47_out, Subtraction, d1_1);
  and and_48 (and_48_out, Subtraction, d1_2);
  xor xor_24 (xor_24_out, and_46_out, xor_17_out);
  and and_49 (and_49_out, and_46_out, not_2_out);
  and and_50 (and_50_out, not_3_out, and_44_out);
  xor xor_25 (xor_25_out, or_8_out, xor_18_out);
  and and_51 (and_51_out, or_8_out, not_4_out);
  and and_52 (and_52_out, not_5_out, and_41_out);
  xor xor_26 (xor_26_out, or_9_out, xor_19_out);
  and and_53 (and_53_out, or_9_out, not_6_out);
  and and_54 (and_54_out, not_7_out, and_40_out);
  xor xor_27 (xor_27_out, or_10_out, xor_20_out);
  and and_55 (and_55_out, or_10_out, not_8_out);
  and and_56 (and_56_out, not_9_out, and_38_out);
  xor xor_28 (xor_28_out, or_11_out, xor_21_out);
  and and_57 (and_57_out, or_11_out, not_10_out);
  and and_58 (and_58_out, not_11_out, and_36_out);
  xor xor_29 (xor_29_out, or_12_out, xor_22_out);
  and and_59 (and_59_out, or_12_out, not_12_out);
  and and_60 (and_60_out, not_13_out, and_33_out);
  xor xor_30 (xor_30_out, or_13_out, xor_23_out);
  and and_61 (and_61_out, or_13_out, not_14_out);
  and and_62 (and_62_out, not_15_out, and_32_out);
  or or_8 (or_8_out, and_49_out, and_50_out);
  or or_9 (or_9_out, and_51_out, and_52_out);
  or or_10 (or_10_out, and_53_out, and_54_out);
  or or_11 (or_11_out, and_55_out, and_56_out);
  or or_12 (or_12_out, and_57_out, and_58_out);
  or or_13 (or_13_out, and_59_out, and_60_out);
  or or_14 (or_14_out, and_61_out, and_62_out);
endmodule
