// Logisim project Half_Sub.circ as structural Verilog: 1 circuit, main circuit main
module main (
  input  A,
  input  B,
  output Diff,
  output Borrow
);

  wire not_1_out;

  not not_1 (not_1_out, A);
  xor xor_1 (Diff, A, B);
  and and_1 (Borrow, not_1_out, B);
endmodule
